// Logisim project cpu.circ as structural Verilog: 4 circuits, main circuit main
module main (
  input  in_1,
  output [31:0] IW_OUT,
  output [31:0] R0,
  output [31:0] R1,
  output [31:0] R,
  output [31:0] R2
);

  wire CLK, IMM___REG, JUMP, PC_WE, Reg_WE;
  wire [1:0] ALU_OP;
  wire [7:0] bitselector_1_out, shifter_1_out;
  wire [23:0] shifter_2_out;
  wire [31:0] adder_1_out, IMM, multiplexer_1_out, multiplexer_2_out, Offset, REG_FILE_pc, REG_FILE_rv1,
       REG_FILE_rv2;

  Clock clock_1 (.out(CLK));
  Shifter #(.shift("lr")) shifter_1 (.in(bitselector_1_out), .\dist (3'b010), .out(shifter_1_out));
  ROM #(.dataWidth(32)) rom_1 (.addr(shifter_1_out), .data(IW_OUT), .sel(1'b1));
  control Control (.IW(IW_OUT), .Reg_WE(Reg_WE), .PC_WE(PC_WE), .JUMP(JUMP), .ALU_OP(ALU_OP), .IMM___REG(IMM___REG));
  assign IMM = {{24{1'b0}}, IW_OUT[7:0]};  // Bit_Extender bit_extender_1
  Shifter #(.width(24)) shifter_2 (.in(IW_OUT[23:0]), .\dist (5'b00010), .out(shifter_2_out));
  assign Offset = {{8{shifter_2_out[23]}}, shifter_2_out};  // Bit_Extender bit_extender_2
  Multiplexer #(.width(32), .enable("false")) multiplexer_1 (
    .in0(R), .in1(IMM), .out(multiplexer_1_out), .sel(IMM___REG));
  BitSelector #(.width(32), .group(8)) bitselector_1 (.in(REG_FILE_pc), .out(bitselector_1_out), .sel(2'b00));
  register_file REG_FILE (
    .CLR(in_1), .WRN(IW_OUT[15:12]), .RV2(REG_FILE_rv2), .RV1(REG_FILE_rv1), .WD(multiplexer_1_out),
    .RD2(IW_OUT[3:0]), .RD1(IW_OUT[19:16]), .PC_IN(multiplexer_2_out), .PC_WE(PC_WE), .PC(REG_FILE_pc),
    .CLK(CLK), .WE(Reg_WE), .R0(R0), .R1(R1), .R2(R2));  // open: CPSR_IN, CPSR_WE, CPSR
  Adder #(.width(32)) adder_1 (.a(REG_FILE_pc), .b(32'h4), .out(adder_1_out));  // open: cin, cout
  alu ALU (.R(R), .A(REG_FILE_rv1), .B(REG_FILE_rv2), .OP(ALU_OP));
  Multiplexer #(.width(32), .enable("false")) multiplexer_2 (
    .in0(adder_1_out), .in1(Offset), .out(multiplexer_2_out), .sel(JUMP));

  // Other names for the same wires on the sheet: RM[3:0] = IW_OUT[3:0]; CLR = in_1; RD[3:0] = IW_OUT[15:12];
  //   RN[3:0] = IW_OUT[19:16]

  // Notes on the sheet:
  //   contents of rom_1 (hex, n*v repeats v):
  //   e3a0d040 e3a00005 ebfffffe eafffffe e24dd004 e58de000 e24dd004 e58d0000 e3500000 1a000001 e3a00001
  //   ea000003 e2400001 ebfffffe e59d1000 e0000190 e28dd004 e59de000 e28dd004 e12fff1e
endmodule

module register_file (
  input  [3:0] RD2,
  input  CLR,
  input  [3:0] RD1,
  input  CLK,
  input  [31:0] WD,
  input  [31:0] CPSR_IN,
  input  [31:0] PC_IN,
  input  [3:0] WRN,
  input  CPSR_WE,
  input  PC_WE,
  input  WE,
  output [31:0] PC,
  output [31:0] R0,
  output [31:0] CPSR,
  output [31:0] RV2,
  output [31:0] R1,
  output [31:0] R2,
  output [31:0] RV1
);

  wire LR_WE, R0_WE, R1_WE, R2_WE, R3_WE, R4_WE, R5_WE, R6_WE, R7_WE, R8_WE, R9_WE, R10_WE, R11_WE, R12_WE,
       SP_WE;
  wire [31:0] LR_Q, PC_Q, R3_Q, R4_Q, R5_Q, R6_Q, R7_Q, R8_Q, R9_Q, R10_Q, R11_Q, R12_Q, SP_Q;

  Register #(.width(32), .trigger("falling")) register_1 (.D(WD), .en(R0_WE), .Q(R0), .clk(CLK), .clr(CLR));
  Register #(.width(32), .trigger("falling")) register_2 (.D(WD), .en(R1_WE), .Q(R1), .clk(CLK), .clr(CLR));
  Register #(.width(32), .trigger("falling")) register_3 (.D(WD), .en(R2_WE), .Q(R2), .clk(CLK), .clr(CLR));
  Register #(.width(32), .trigger("falling")) register_4 (.D(WD), .en(R3_WE), .Q(R3_Q), .clk(CLK), .clr(CLR));
  Register #(.width(32), .trigger("falling")) register_5 (.D(WD), .en(R4_WE), .Q(R4_Q), .clk(CLK), .clr(CLR));
  Register #(.width(32), .trigger("falling")) register_6 (.D(WD), .en(R5_WE), .Q(R5_Q), .clk(CLK), .clr(CLR));
  Register #(.width(32), .trigger("falling")) register_7 (.D(WD), .en(R6_WE), .Q(R6_Q), .clk(CLK), .clr(CLR));
  Register #(.width(32), .trigger("falling")) register_8 (.D(WD), .en(R7_WE), .Q(R7_Q), .clk(CLK), .clr(CLR));
  Register #(.width(32), .trigger("falling")) register_9 (.D(WD), .en(R8_WE), .Q(R8_Q), .clk(CLK), .clr(CLR));
  Decoder #(.select(4)) decoder_1 (
    .out0(R0_WE), .out1(R1_WE), .out2(R2_WE), .out3(R3_WE), .out4(R4_WE), .out5(R5_WE), .out6(R6_WE),
    .out7(R7_WE), .out8(R8_WE), .out9(R9_WE), .out10(R10_WE), .out11(R11_WE), .out12(R12_WE), .out13(SP_WE),
    .out14(LR_WE), .sel(WRN), .en(WE));  // open: out15
  Register #(.width(32), .trigger("falling")) register_10 (.D(WD), .en(R9_WE), .Q(R9_Q), .clk(CLK), .clr(CLR));
  Register #(.width(32), .trigger("falling")) register_11 (.D(WD), .en(R10_WE), .Q(R10_Q), .clk(CLK), .clr(CLR));
  Register #(.width(32), .trigger("falling")) register_12 (.D(WD), .en(R11_WE), .Q(R11_Q), .clk(CLK), .clr(CLR));
  Register #(.width(32), .trigger("falling")) register_13 (.D(WD), .en(R12_WE), .Q(R12_Q), .clk(CLK), .clr(CLR));
  Register #(.width(32), .trigger("falling")) register_14 (.D(WD), .en(SP_WE), .Q(SP_Q), .clk(CLK), .clr(CLR));
  Register #(.width(32), .trigger("falling")) register_15 (.D(WD), .en(LR_WE), .Q(LR_Q), .clk(CLK), .clr(CLR));
  Register #(.width(32), .trigger("falling")) register_16 (.D(PC_IN), .en(PC_WE), .Q(PC), .clk(CLK), .clr(CLR));
  Register #(.width(32), .trigger("falling")) register_17 (.D(CPSR_IN), .en(CPSR_WE), .Q(CPSR), .clk(CLK), .clr(CLR));
  Multiplexer #(.select(4), .width(32), .enable("false")) multiplexer_1 (
    .in0(R0), .in1(R1), .in2(R2), .in3(R3_Q), .in4(R4_Q), .in5(R5_Q), .in6(R6_Q), .in7(R7_Q), .in8(R8_Q),
    .in9(R9_Q), .in10(R10_Q), .in11(R11_Q), .in12(R12_Q), .in13(SP_Q), .in14(LR_Q), .in15(PC_Q), .out(RV2),
    .sel(RD2));
  Multiplexer #(.select(4), .width(32), .enable("false")) multiplexer_2 (
    .in0(R0), .in1(R1), .in2(R2), .in3(R3_Q), .in4(R4_Q), .in5(R5_Q), .in6(R6_Q), .in7(R7_Q), .in8(R8_Q),
    .in9(R9_Q), .in10(R10_Q), .in11(R11_Q), .in12(R12_Q), .in13(SP_Q), .in14(LR_Q), .in15(PC_Q), .out(RV1),
    .sel(RD1));

  // Other names for the same wires on the sheet: R0_Q[31:0] = R0; R1_Q[31:0] = R1; R2_Q[31:0] = R2
endmodule

module alu (
  input  [1:0] OP,
  input  [31:0] A,
  input  [31:0] B,
  output [31:0] R
);

  wire [31:0] adder_1_out, multiplier_1_out, subtractor_1_out;

  Adder #(.width(32)) adder_1 (.a(A), .b(B), .out(adder_1_out));  // open: cin, cout
  Subtractor #(.width(32)) subtractor_1 (.a(A), .b(B), .out(subtractor_1_out));  // open: bin, bout
  Multiplier #(.width(32)) multiplier_1 (.a(A), .b(B), .out(multiplier_1_out));  // open: cin, cout
  Multiplexer #(.select(2), .width(32), .enable("false")) multiplexer_1 (
    .in0(adder_1_out), .in1(subtractor_1_out), .in2(multiplier_1_out), .out(R), .sel(OP));  // open: in3
endmodule

module control (
  input  [31:0] IW,
  output Reg_WE,
  output PC_WE,
  output JUMP,
  output [1:0] ALU_OP,
  output IMM___REG
);

  wire ADD_out, B_OFFSET_out, MOV_IMM_out, or_4_out;

  and MOV_IMM (MOV_IMM_out, ~IW[27], ~IW[26], IW[25], IW[24], IW[23], ~IW[22], IW[21], ~IW[20]);  // AND_Gate
  and B_OFFSET (B_OFFSET_out, IW[27], ~IW[26], IW[25], ~IW[24]);  // AND_Gate
  and ADD (ADD_out, ~IW[27], ~IW[26], ~IW[25], ~IW[24], IW[23], ~IW[22], ~IW[21], ~IW[20]);  // AND_Gate
  or or_1 (Reg_WE, MOV_IMM_out, ADD_out);
  or or_2 (PC_WE, MOV_IMM_out, ADD_out);
  buf or_3 (JUMP, B_OFFSET_out);  // OR_Gate
  buf or_4 (or_4_out, ADD_out);  // OR_Gate
  buf or_5 (IMM___REG, MOV_IMM_out);  // OR_Gate
  not not_1 (ALU_OP[0], or_4_out);

  assign ALU_OP[1] = 1'b0;
endmodule
